# Fritzing sketch wiring (saved by Fritzing 0.9.2b)

parts:
  Raspberry_Pi1 = Raspberry Pi 2
  J1 = Basic Servo
  Composant1 = Arduino Uno (Rev3)
  J2 = Basic Servo
  LED1 = LED - 5mm [color="Red (633nm)" package="5 mm [THT]"]
  R1 = Resistor [tolerance=±5% resistance=220 package=THT]

nets (from the breadboard view):
  N1: Raspberry_Pi1.GPIO3, Composant1.A5/SCL
  GND: Raspberry_Pi1.GND, J1.gnd, Composant1.GND, J2.gnd, LED1.cathode
  N2: Raspberry_Pi1.5V, Composant1.A4/SDA
  VCC: J1.vcc, Composant1.5V, J2.vcc, R1.Pin_1
  N3: J1.pulse, Composant1.D9_PWM
  N4: Composant1.D10_PWM/SS, J2.pulse
  N5: LED1.anode, R1.Pin_0
